// Logisim project PROJECT.circ as structural Verilog: 15 circuits, main circuit main
module main (
  input  [3:0] INPR
);

  wire and_1_out, clock_1_out, control_unit_1_dr_ld, control_unit_1_hlt, control_unit_1_outr_ld, not_1_out;
  wire [1:0] control_unit_1_ir_ld, control_unit_1_memory_ld;
  wire [2:0] control_unit_1_ar_inc, control_unit_1_pc_inc;
  wire [3:0] AC_out_6, alu_1_output, AR_out_6, control_unit_1_ac_inc, controlled_buffer_1_out,
       controlled_buffer_1_out_2, DR_out_6, OUTR_out_6, PC_out_6;
  wire [6:0] control_unit_1_alu_and;
  wire [7:0] IR_output, ram_1_data;

  Clock clock_1 (.out(clock_1_out));
  not not_1 (not_1_out, control_unit_1_hlt);
  and and_1 (and_1_out, not_1_out, clock_1_out);
  CONTROL_UNIT control_unit_1 (
    .IR_4___7(IR_output[7:4]), .CLK(and_1_out), .PC_BUS(control_unit_1_pc_inc[2]),
    .PC_INC(control_unit_1_pc_inc[0]), .PC_LD(control_unit_1_pc_inc[1]), .AR_BUS(control_unit_1_ar_inc[2]),
    .AR_LD(control_unit_1_ar_inc[1]), .AR_INC(control_unit_1_ar_inc[0]), .DR_LD(control_unit_1_dr_ld),
    .AC_BUS(control_unit_1_ac_inc[3]), .AC_INC(control_unit_1_ac_inc[0]), .AC_LD(control_unit_1_ac_inc[1]),
    .AC_CLR(control_unit_1_ac_inc[2]), .MEMORY_BUS(control_unit_1_memory_ld[1]),
    .MEMORY_LD(control_unit_1_memory_ld[0]), .IR_BUS(control_unit_1_ir_ld[1]),
    .IR_LD(control_unit_1_ir_ld[0]), .ALU_AND(control_unit_1_alu_and[0]),
    .ALU_ADD(control_unit_1_alu_and[1]), .ALU_CMA(control_unit_1_alu_and[2]),
    .ALU_LD__DR(control_unit_1_alu_and[3]), .ALU_LD__INPR(control_unit_1_alu_and[4]),
    .ALU_CIR(control_unit_1_alu_and[5]), .ALU_CIL(control_unit_1_alu_and[6]),
    .OUTR_LD(control_unit_1_outr_ld), .HLT(control_unit_1_hlt));
  ALU alu_1 (
    .AC(AC_out_6), .DR(DR_out_6), .INPR(INPR), .AND(control_unit_1_alu_and[0]),
    .ADD(control_unit_1_alu_and[1]), .CMA(control_unit_1_alu_and[2]), .LD_DR(control_unit_1_alu_and[3]),
    .LD_INPR(control_unit_1_alu_and[4]), .CIR(control_unit_1_alu_and[5]), .CIL(control_unit_1_alu_and[6]),
    .\output (alu_1_output));  // open: cin, E_AC_0, cout, E_AC_3
  RAM #(.addrWidth(4), .bus("separate")) ram_1 (
    .addr(AR_out_6), .din({controlled_buffer_1_out_2, controlled_buffer_1_out}), .data(ram_1_data),
    .str(control_unit_1_memory_ld[0]), .clk(and_1_out));  // open: sel, ld, clr
  // Probe on AR_out_6
  _4_bit_reg AR (
    .INPUT(controlled_buffer_1_out), .CLK(and_1_out), .INC(control_unit_1_ar_inc[0]),
    .LD(control_unit_1_ar_inc[1]), .out_6(AR_out_6));  // open: CLR
  // Probe on PC_out_6
  _4_bit_reg PC (
    .INPUT(controlled_buffer_1_out), .CLK(and_1_out), .INC(control_unit_1_pc_inc[0]),
    .LD(control_unit_1_pc_inc[1]), .out_6(PC_out_6));  // open: CLR
  // Probe on DR_out_6
  _4_bit_reg DR (
    .INPUT(controlled_buffer_1_out), .CLK(and_1_out), .LD(control_unit_1_dr_ld), .out_6(DR_out_6));  // open: INC, CLR
  // Probe on AC_out_6
  _4_bit_reg AC (
    .INPUT(alu_1_output), .CLK(and_1_out), .INC(control_unit_1_ac_inc[0]), .LD(control_unit_1_ac_inc[1]),
    .CLR(control_unit_1_ac_inc[2]), .out_6(AC_out_6));
  // Probe on IR_output
  _8_bit_reg IR (
    .Input({controlled_buffer_1_out_2, controlled_buffer_1_out}), .CLK(and_1_out),
    .LD(control_unit_1_ir_ld[0]), .Output(IR_output));
  _4_bit_reg OUTR (
    .INPUT(controlled_buffer_1_out), .CLK(and_1_out), .LD(control_unit_1_outr_ld), .out_6(OUTR_out_6));  // open: INC, CLR
  // Probe on OUTR_out_6
  assign {controlled_buffer_1_out_2, controlled_buffer_1_out} = control_unit_1_memory_ld[1] ? ram_1_data : 8'bz;  // Controlled_Buffer controlled_buffer_1
  assign {controlled_buffer_1_out_2, controlled_buffer_1_out} = control_unit_1_ar_inc[2] ? {4'b0000, AR_out_6} : 8'bz;  // Controlled_Buffer controlled_buffer_2
  assign {controlled_buffer_1_out_2, controlled_buffer_1_out} = control_unit_1_pc_inc[2] ? {4'b0000, PC_out_6} : 8'bz;  // Controlled_Buffer controlled_buffer_3
  assign {controlled_buffer_1_out_2, controlled_buffer_1_out} = control_unit_1_ac_inc[3] ? {4'b0000, AC_out_6} : 8'bz;  // Controlled_Buffer controlled_buffer_4
  assign {controlled_buffer_1_out_2, controlled_buffer_1_out} = control_unit_1_ir_ld[1] ? IR_output : 8'bz;  // Controlled_Buffer controlled_buffer_5
endmodule

// CONTROL_UNITl
module CONTROL_UNIT (
  input  [3:0] IR_4___7,
  input  CLK,
  output PC_BUS,
  output PC_INC,
  output PC_LD,
  output AR_BUS,
  output AR_LD,
  output AR_INC,
  output DR_LD,
  output AC_BUS,
  output AC_INC,
  output AC_LD,
  output AC_CLR,
  output MEMORY_BUS,
  output MEMORY_LD,
  output IR_BUS,
  output IR_LD,
  output ALU_AND,
  output ALU_ADD,
  output ALU_CMA,
  output ALU_LD__DR,
  output ALU_LD__INPR,
  output ALU_CIR,
  output ALU_CIL,
  output OUTR_LD,
  output HLT
);

  wire d_ff_1_q, decoder_1_out8, decoder_1_out15, sc_clear_1_sc_clear_ld;
  wire [0:0] decoder_2_out0;
  wire [1:0] decoder_2_out2, decoder_2_out4;
  wire [2:0] counter_1_q, decoder_1_out4;
  wire [3:3] decoder_1_out3;
  wire [6:0] decoder_1_out9;
  wire [7:2] decoder_1_out7;

  Counter #(.width(3), .max('h7), .trigger("falling")) counter_1 (
    .Q(counter_1_q), .clk(CLK), .clr(d_ff_1_q));  // open: load, D, count, carry
  D_Flip_Flop d_ff_1 (.clk(CLK), .D(sc_clear_1_sc_clear_ld), .Q(d_ff_1_q));  // open: Qn, preset, en, reset
  Decoder #(.select(4)) decoder_1 (
    .out0(decoder_1_out9[6]), .out1(decoder_1_out9[5]), .out2(decoder_1_out9[4]), .out3(decoder_1_out3[3]),
    .out4(decoder_1_out4[0]), .out5(decoder_1_out4[1]), .out6(decoder_1_out4[2]), .out7(decoder_1_out7[2]),
    .out8(decoder_1_out8), .out9(decoder_1_out9[3]), .out10(decoder_1_out7[3]), .out11(decoder_1_out9[2]),
    .out12(decoder_1_out9[1]), .out13(decoder_1_out9[0]), .out14(decoder_1_out7[7]), .out15(decoder_1_out15),
    .sel(IR_4___7));  // open: en
  Decoder #(.select(3)) decoder_2 (
    .out0(decoder_2_out0[0]), .out1(decoder_2_out2[0]), .out2(decoder_2_out2[1]), .out3(decoder_2_out4[1]),
    .out4(decoder_2_out4[0]), .sel(counter_1_q));  // open: out5, out6, out7, en
  SC_CLEAR sc_clear_1 (
    .T3(decoder_2_out4[1]), .T4(decoder_2_out4[0]), .D0(decoder_1_out9[6]), .D1(decoder_1_out9[5]),
    .D2(decoder_1_out9[4]), .D3(decoder_1_out3[3]), .D4(decoder_1_out4[0]), .D5(decoder_1_out4[1]),
    .D6(decoder_1_out4[2]), .D7(decoder_1_out7[2]), .D8(decoder_1_out8), .D9(decoder_1_out9[3]),
    .D10(decoder_1_out7[3]), .D11(decoder_1_out9[2]), .D12(decoder_1_out9[1]), .D13(decoder_1_out9[0]),
    .D14(decoder_1_out7[7]), .D15(decoder_1_out15), .SC_CLEAR_LD(sc_clear_1_sc_clear_ld), .HLT(HLT));
  AR ar_1 (
    .T0(decoder_2_out0[0]), .T2(decoder_2_out2[1]), .T3(decoder_2_out4[1]), .T4(decoder_2_out4[0]),
    .D4(decoder_1_out4[0]), .D5(decoder_1_out4[1]), .AR_BUS(AR_BUS), .AR_LD(AR_LD), .AR_INC(AR_INC));
  DR dr_1 (
    .T3(decoder_2_out4[1]), .D0(decoder_1_out9[6]), .D1(decoder_1_out9[5]), .D2(decoder_1_out9[4]),
    .DR_LD(DR_LD));
  CU_IR cu_ir_1 (.T1(decoder_2_out2[0]), .T2(decoder_2_out2[1]), .IR_BUS(IR_BUS), .IR_LD(IR_LD));
  CU_ALU cu_alu_1 (
    .T3(decoder_2_out4[1]), .T4(decoder_2_out4[0]), .D0(decoder_1_out9[6]), .D1(decoder_1_out9[5]),
    .D2(decoder_1_out9[4]), .D9(decoder_1_out9[3]), .D11(decoder_1_out9[2]), .D12(decoder_1_out9[1]),
    .D13(decoder_1_out9[0]), .ALU_AND(ALU_AND), .ALU_ADD(ALU_ADD), .ALU_CMA(ALU_CMA),
    .ALU_LD__DR(ALU_LD__DR), .ALU_LD__INPR(ALU_LD__INPR), .ALU_LD_CIR(ALU_CIR), .ALU_LD_CIL(ALU_CIL));
  OUTR outr_1 (.T3(decoder_2_out4[1]), .D14(decoder_1_out7[7]), .OUTR_LD(OUTR_LD));
  PC pc_1 (
    .T0(decoder_2_out0[0]), .T1(decoder_2_out2[0]), .T3(decoder_2_out4[1]), .T4(decoder_2_out4[0]),
    .D4(decoder_1_out4[0]), .D5(decoder_1_out4[1]), .D6(decoder_1_out4[2]), .PC_BUS(PC_BUS), .PC_INC(PC_INC),
    .PC_LD(PC_LD));
  AC ac_1 (
    .T3(decoder_2_out4[1]), .T4(decoder_2_out4[0]), .D2(decoder_1_out9[4]), .D3(decoder_1_out3[3]),
    .D7(decoder_1_out7[2]), .D10(decoder_1_out7[3]), .D11(decoder_1_out9[2]), .D12(decoder_1_out9[1]),
    .D13(decoder_1_out9[0]), .D14(decoder_1_out7[7]), .AC_BUS(AC_BUS), .AC_INC(AC_INC), .AC_LD(AC_LD),
    .AC_CLR(AC_CLR));
  memory memory_1 (
    .T1(decoder_2_out2[0]), .T3(decoder_2_out4[1]), .D0(decoder_1_out9[6]), .D1(decoder_1_out9[5]),
    .D2(decoder_1_out9[4]), .D3(decoder_1_out3[3]), .D5(decoder_1_out4[1]), .D6(decoder_1_out4[2]),
    .MEMORY_BUS(MEMORY_BUS), .MEMORY_LD(MEMORY_LD));

  // Notes on the sheet:
  //   D
  //   T
endmodule

module PC (
  input  T0,
  input  T1,
  input  T3,
  input  T4,
  input  D4,
  input  D5,
  input  D6,
  output PC_BUS,
  output PC_INC,
  output PC_LD
);

  wire and_1_out, and_2_out, and_3_out, and_4_out;

  and and_1 (and_1_out, T3, D5);
  and and_2 (and_2_out, T3, D4);
  and and_3 (and_3_out, T4, D5);
  and and_4 (and_4_out, T3, D6);
  or or_1 (PC_BUS, and_1_out, T0);
  or or_2 (PC_LD, and_2_out, and_3_out, and_4_out);

  assign PC_INC = T1;
endmodule

module AR (
  input  T0,
  input  T2,
  input  T3,
  input  T4,
  input  D4,
  input  D5,
  output AR_BUS,
  output AR_LD,
  output AR_INC
);

  wire and_1_out, and_2_out;

  and and_1 (and_1_out, D4, T3);
  and and_2 (and_2_out, D5, T4);
  and and_3 (AR_INC, T3, D5);
  or or_1 (AR_BUS, and_1_out, and_2_out);
  or or_2 (AR_LD, T0, T2);
endmodule

module DR (
  input  T3,
  input  D0,
  input  D1,
  input  D2,
  output DR_LD
);

  wire and_1_out, and_2_out, and_3_out;

  and and_1 (and_1_out, D0, T3);
  and and_2 (and_2_out, D1, T3);
  and and_3 (and_3_out, D2, T3);
  or or_1 (DR_LD, and_1_out, and_2_out, and_3_out);
endmodule

module AC (
  input  T3,
  input  T4,
  input  D2,
  input  D3,
  input  D7,
  input  D10,
  input  D11,
  input  D12,
  input  D13,
  input  D14,
  output AC_BUS,
  output AC_INC,
  output AC_LD,
  output AC_CLR
);

  wire and_1_out, and_2_out, and_4_out, and_5_out, and_6_out, and_7_out;

  and and_1 (and_1_out, T3, D3);
  and and_2 (and_2_out, T3, D14);
  and and_3 (AC_INC, T3, D10);
  and and_4 (and_4_out, T4, D2);
  and and_5 (and_5_out, T3, D11);
  and and_6 (and_6_out, T3, D12);
  and and_7 (and_7_out, T3, D13);
  and and_8 (AC_CLR, T3, D7);
  or or_1 (AC_BUS, and_1_out, and_2_out);
  or or_2 (AC_LD, and_4_out, and_5_out, and_6_out, and_7_out);
endmodule

// MEMORY
module memory (
  input  T1,
  input  T3,
  input  D0,
  input  D1,
  input  D2,
  input  D3,
  input  D5,
  input  D6,
  output MEMORY_BUS,
  output MEMORY_LD
);

  wire and_1_out, and_2_out, and_3_out, and_4_out, and_5_out, and_6_out;

  and and_1 (and_1_out, T3, D0);
  and and_2 (and_2_out, T3, D1);
  and and_3 (and_3_out, T3, D2);
  and and_4 (and_4_out, T3, D6);
  and and_5 (and_5_out, T3, D3);
  and and_6 (and_6_out, T3, D5);
  or or_1 (MEMORY_LD, and_5_out, and_6_out);
  or or_2 (MEMORY_BUS, T1, and_1_out, and_2_out, and_3_out, and_4_out);
endmodule

module SC_CLEAR (
  input  T3,
  input  T4,
  input  D0,
  input  D1,
  input  D2,
  input  D3,
  input  D4,
  input  D5,
  input  D6,
  input  D7,
  input  D8,
  input  D9,
  input  D10,
  input  D11,
  input  D12,
  input  D13,
  input  D14,
  input  D15,
  output SC_CLEAR_LD,
  output HLT
);

  wire and_1_out, and_2_out, or_1_out, or_2_out;

  or or_1 (or_1_out, D15, D14, D13, D12, D11, D10, D9, D8, D7, D6, D4, D3);
  or or_2 (or_2_out, D5, D2, D1, D0);
  and and_1 (and_1_out, or_1_out, T3);
  and and_2 (and_2_out, or_2_out, T4);
  or or_3 (SC_CLEAR_LD, and_1_out, and_2_out);

  assign HLT = D15;
endmodule

// IR
module CU_IR (
  input  T1,
  input  T2,
  output IR_BUS,
  output IR_LD
);


  assign IR_BUS = T2;
  assign IR_LD = T1;
endmodule

module ALU (
  input  cin,
  input  E_AC_0,
  input  [3:0] AC,
  input  [3:0] DR,
  input  [3:0] INPR,
  input  AND,
  input  ADD,
  input  CMA,
  input  LD_DR,
  input  LD_INPR,
  input  CIR,
  input  CIL,
  input  E_AC_3,
  output [3:0] \output ,
  output cout
);

  wire n1_bit_alu_1_cout, n1_bit_alu_2_cout, n1_bit_alu_3_cout;

  _1_bit_alu u_1_bit_alu_1 (
    .AND(AND), .ADD(ADD), .CMA(CMA), .LD_DR(LD_DR), .LD_INPR(LD_INPR), .CIR(CIR), .CIL(CIL), .AC_i_1(E_AC_0),
    .AC_i_1_2(AC[1]), .INPR(INPR[0]), .DR(DR[0]), .AC(AC[0]), .cin(cin), .cout(n1_bit_alu_1_cout),
    .output_AC(E_AC_0));
  _1_bit_alu u_1_bit_alu_2 (
    .AND(AND), .ADD(ADD), .CMA(CMA), .LD_DR(LD_DR), .LD_INPR(LD_INPR), .CIR(CIR), .CIL(CIL), .AC_i_1(AC[0]),
    .AC_i_1_2(AC[2]), .INPR(INPR[1]), .DR(DR[1]), .AC(AC[1]), .cin(n1_bit_alu_1_cout),
    .cout(n1_bit_alu_2_cout), .output_AC(\output [1]));
  _1_bit_alu u_1_bit_alu_3 (
    .AND(AND), .ADD(ADD), .CMA(CMA), .LD_DR(LD_DR), .LD_INPR(LD_INPR), .CIR(CIR), .CIL(CIL), .AC_i_1(AC[1]),
    .AC_i_1_2(AC[3]), .INPR(INPR[2]), .DR(DR[2]), .AC(AC[2]), .cin(n1_bit_alu_2_cout),
    .cout(n1_bit_alu_3_cout), .output_AC(\output [2]));
  _1_bit_alu u_1_bit_alu_4 (
    .AND(AND), .ADD(ADD), .CMA(CMA), .LD_DR(LD_DR), .LD_INPR(LD_INPR), .CIR(CIR), .CIL(CIL), .AC_i_1(AC[2]),
    .AC_i_1_2(E_AC_3), .INPR(INPR[3]), .DR(DR[3]), .AC(AC[3]), .cin(n1_bit_alu_3_cout), .cout(cout),
    .output_AC(\output [3]));

  assign \output [0] = E_AC_0;
endmodule

module OUTR (
  input  T3,
  input  D14,
  output OUTR_LD
);

  and and_1 (OUTR_LD, D14, T3);
endmodule

module _4_bit_reg (
  input  INC,
  input  LD,
  input  [3:0] INPUT,
  input  CLR,
  input  CLK,
  output [3:0] out_6
);

  wire and_1_out, and_2_out, and_3_out, and_4_out, and_5_out, and_6_out, and_7_out, and_8_out, and_9_out,
       and_10_out, and_11_out, and_12_out, not_1_out, not_2_out, not_3_out, not_4_out, not_5_out, not_6_out,
       or_1_out, or_2_out, or_3_out, or_4_out, or_5_out, or_6_out, or_7_out, or_8_out;

  not not_1 (not_1_out, LD);
  and and_1 (and_1_out, INC, not_1_out);
  not not_2 (not_2_out, not_1_out);
  not not_3 (not_3_out, INPUT[0]);
  not not_4 (not_4_out, INPUT[1]);
  not not_5 (not_5_out, INPUT[2]);
  not not_6 (not_6_out, INPUT[3]);
  and and_2 (and_2_out, not_2_out, INPUT[0]);
  and and_3 (and_3_out, not_2_out, not_3_out);
  and and_4 (and_4_out, not_2_out, INPUT[1]);
  and and_5 (and_5_out, not_2_out, not_4_out);
  and and_6 (and_6_out, not_2_out, INPUT[2]);
  and and_7 (and_7_out, not_2_out, not_5_out);
  and and_8 (and_8_out, not_2_out, INPUT[3]);
  and and_9 (and_9_out, not_2_out, not_6_out);
  or or_1 (or_1_out, and_2_out, and_1_out);
  or or_2 (or_2_out, and_3_out, and_1_out);
  or or_3 (or_3_out, and_4_out, and_10_out);
  and and_10 (and_10_out, and_1_out, out_6[0]);
  or or_4 (or_4_out, and_10_out, and_5_out);
  or or_5 (or_5_out, and_6_out, and_11_out);
  and and_11 (and_11_out, and_1_out, out_6[0], out_6[1]);
  or or_6 (or_6_out, and_11_out, and_7_out);
  or or_7 (or_7_out, and_8_out, and_12_out);
  and and_12 (and_12_out, and_1_out, out_6[0], out_6[1], out_6[2]);
  or or_8 (or_8_out, and_12_out, and_9_out);
  J_K_Flip_Flop j_k_ff_1 (.J(or_1_out), .clk(CLK), .K(or_2_out), .Q(out_6[0]), .reset(CLR));  // open: Qn, preset, en
  J_K_Flip_Flop j_k_ff_2 (.J(or_3_out), .clk(CLK), .K(or_4_out), .Q(out_6[1]), .reset(CLR));  // open: Qn, preset, en
  J_K_Flip_Flop j_k_ff_3 (.J(or_5_out), .clk(CLK), .K(or_6_out), .Q(out_6[2]), .reset(CLR));  // open: Qn, preset, en
  J_K_Flip_Flop j_k_ff_4 (.J(or_7_out), .clk(CLK), .K(or_8_out), .Q(out_6[3]), .reset(CLR));  // open: Qn, preset, en
endmodule

module _8_bit_reg (
  input  [7:0] Input,
  input  CLK,
  input  LD,
  output [7:0] Output
);

  _4_bit_reg u_4_bit_reg_1 (.INPUT(Input[3:0]), .CLK(CLK), .LD(LD), .out_6(Output[3:0]));  // open: INC, CLR
  _4_bit_reg u_4_bit_reg_2 (.INPUT(Input[7:4]), .CLK(CLK), .LD(LD), .out_6(Output[7:4]));  // open: INC, CLR
endmodule

// ALU
module CU_ALU (
  input  T3,
  input  T4,
  input  D0,
  input  D1,
  input  D2,
  input  D9,
  input  D11,
  input  D12,
  input  D13,
  output ALU_AND,
  output ALU_ADD,
  output ALU_CMA,
  output ALU_LD__DR,
  output ALU_LD__INPR,
  output ALU_LD_CIR,
  output ALU_LD_CIL
);

  and and_1 (ALU_AND, T4, D0);
  and and_2 (ALU_ADD, T4, D1);
  and and_3 (ALU_CMA, T3, D9);
  and and_4 (ALU_LD__DR, T4, D2);
  and and_5 (ALU_LD__INPR, T3, D13);
  and and_6 (ALU_LD_CIR, T3, D11);
  and and_7 (ALU_LD_CIL, T3, D12);
endmodule

// ALU
module _1_bit_alu (
  input  INPR,
  input  DR,
  input  AC,
  input  AND,
  input  cin,
  input  ADD,
  input  CMA,
  input  LD_DR,
  input  LD_INPR,
  input  CIR,
  input  CIL,
  input  AC_i_1,
  input  AC_i_1_2,
  output cout,
  output output_AC
);

  wire add_out, adder_1_out, and_out, comp_out, Id_DR_out, Id_INPR_out, not_1_out, shl_out, shr_out;

  Adder #(.width(1)) adder_1 (.a(AC), .b(DR), .out(adder_1_out), .cin(cin), .cout(cout));
  not not_1 (not_1_out, AC);
  and u_and (and_out, AND, AC, DR);
  and u_add (add_out, ADD, adder_1_out);
  and comp (comp_out, CMA, not_1_out);
  and Id_DR (Id_DR_out, LD_DR, DR);
  and Id_INPR (Id_INPR_out, LD_INPR, INPR);
  and shr (shr_out, CIR, AC_i_1_2);
  and shl (shl_out, CIL, AC_i_1);
  or or_1 (output_AC, and_out, add_out, comp_out, Id_DR_out, Id_INPR_out, shr_out, shl_out);
endmodule
